// Logisim project tb-pipeline.circ as structural Verilog: 4 circuits, main circuit tester
module tester (
  output [31:0] pc_w,
  output [31:0] pc_m,
  output RegWrite,
  output [4:0] RegAddr,
  output [31:0] RegData,
  output MemWrite,
  output [31:0] MemAddr,
  output [31:0] MemData,
  output [15:0] out_9,
  output halt
);

  wire clock_1_out, main_1_p1;
  wire [3:0] hex2dec_1_hi, hex2dec_1_lo, mask32_1_out_2, mask32_1_out_3, mask32_2_out_2, mask32_2_out_3,
       mask32_2_out_4, mask32_3_out, mask32_3_out_3, mask32_3_out_4;
  wire [4:0] mask5_1_out;
  wire [19:0] mask32_2_out;
  wire [23:0] mask32_1_out;
  wire [23:4] mask32_3_out_2;

  Clock clock_1 (.out(clock_1_out));
  // test_main main_1: pin names not known; wires that end beside it: main_1_p1, pc_w, pc_m, RegWrite, RegAddr, RegData, MemWrite, MemAddr, MemData
  Comparator #(.width(16), .mode("unsigned")) comparator_1 (.a(16'h1), .b(out_9), .gt(main_1_p1));  // open: eq, lt
  Counter #(.width(16), .max('h800), .ongoal("stay")) counter_1 (
    .Q(out_9), .carry(halt), .clk(clock_1_out));  // open: load, D, count, clr
  Hex_Digit_Display hex_digit_display_1 (.value(mask32_1_out_2));  // open: dp
  Hex_Digit_Display hex_digit_display_2 (.value(mask32_1_out_3));  // open: dp
  mask5 mask5_1 (.in(RegAddr), .en(RegWrite), .out(mask5_1_out));
  Hex_Digit_Display hex_digit_display_3 (.value(mask32_1_out[19:16]));  // open: dp
  Hex_Digit_Display hex_digit_display_4 (.value(mask32_1_out[23:20]));  // open: dp
  mask32 mask32_1 (.in(MemAddr), .en(MemWrite), .out({mask32_1_out_3, mask32_1_out_2, mask32_1_out}));
  Hex_Digit_Display hex_digit_display_5 (.value(hex2dec_1_lo));  // open: dp
  Hex_Digit_Display hex_digit_display_6 (.value(hex2dec_1_hi));  // open: dp
  hex2dec hex2dec_1 (.hex5(mask5_1_out), .hi(hex2dec_1_hi), .lo(hex2dec_1_lo));
  Hex_Digit_Display hex_digit_display_7 (.value(mask32_1_out[15:12]));  // open: dp
  Hex_Digit_Display hex_digit_display_8 (.value(mask32_1_out[11:8]));  // open: dp
  Hex_Digit_Display hex_digit_display_9 (.value(pc_w[31:28]));  // open: dp
  Hex_Digit_Display hex_digit_display_10 (.value(pc_w[27:24]));  // open: dp
  Hex_Digit_Display hex_digit_display_11 (.value(pc_m[31:28]));  // open: dp
  Hex_Digit_Display hex_digit_display_12 (.value(pc_m[27:24]));  // open: dp
  Hex_Digit_Display hex_digit_display_13 (.value(mask32_1_out[3:0]));  // open: dp
  Hex_Digit_Display hex_digit_display_14 (.value(mask32_1_out[7:4]));  // open: dp
  LED u_RegWrite (.in(RegWrite));
  Hex_Digit_Display hex_digit_display_15 (.value(pc_w[23:20]));  // open: dp
  Hex_Digit_Display hex_digit_display_16 (.value(pc_w[19:16]));  // open: dp
  Hex_Digit_Display hex_digit_display_17 (.value(pc_m[23:20]));  // open: dp
  Hex_Digit_Display hex_digit_display_18 (.value(pc_m[19:16]));  // open: dp
  LED u_MemWrite (.in(MemWrite));
  Hex_Digit_Display hex_digit_display_19 (.value(pc_w[11:8]));  // open: dp
  Hex_Digit_Display hex_digit_display_20 (.value(pc_w[15:12]));  // open: dp
  Hex_Digit_Display hex_digit_display_21 (.value(mask32_2_out_3));  // open: dp
  Hex_Digit_Display hex_digit_display_22 (.value(mask32_2_out_4));  // open: dp
  Hex_Digit_Display hex_digit_display_23 (.value(pc_m[11:8]));  // open: dp
  Hex_Digit_Display hex_digit_display_24 (.value(pc_m[15:12]));  // open: dp
  Hex_Digit_Display hex_digit_display_25 (.value(pc_w[3:0]));  // open: dp
  Hex_Digit_Display hex_digit_display_26 (.value(pc_w[7:4]));  // open: dp
  Hex_Digit_Display hex_digit_display_27 (.value(mask32_2_out[19:16]));  // open: dp
  Hex_Digit_Display hex_digit_display_28 (.value(mask32_2_out_2));  // open: dp
  mask32 mask32_2 (.in(RegData), .en(RegWrite), .out({mask32_2_out_4, mask32_2_out_3, mask32_2_out_2, mask32_2_out}));
  Hex_Digit_Display hex_digit_display_29 (.value(pc_m[3:0]));  // open: dp
  Hex_Digit_Display hex_digit_display_30 (.value(pc_m[7:4]));  // open: dp
  Hex_Digit_Display hex_digit_display_31 (.value(mask32_3_out_4));  // open: dp
  Hex_Digit_Display hex_digit_display_32 (.value(mask32_3_out_3));  // open: dp
  Hex_Digit_Display hex_digit_display_33 (.value(mask32_2_out[11:8]));  // open: dp
  Hex_Digit_Display hex_digit_display_34 (.value(mask32_2_out[15:12]));  // open: dp
  Hex_Digit_Display hex_digit_display_35 (.value(mask32_3_out_2[23:20]));  // open: dp
  Hex_Digit_Display hex_digit_display_36 (.value(mask32_3_out_2[19:16]));  // open: dp
  mask32 mask32_3 (.in(MemData), .en(MemWrite), .out({mask32_3_out_4, mask32_3_out_3, mask32_3_out_2, mask32_3_out}));
  Hex_Digit_Display hex_digit_display_37 (.value(mask32_2_out[3:0]));  // open: dp
  Hex_Digit_Display hex_digit_display_38 (.value(mask32_2_out[7:4]));  // open: dp
  Hex_Digit_Display hex_digit_display_39 (.value(mask32_3_out_2[11:8]));  // open: dp
  Hex_Digit_Display hex_digit_display_40 (.value(mask32_3_out_2[15:12]));  // open: dp
  Hex_Digit_Display hex_digit_display_41 (.value(mask32_3_out));  // open: dp
  Hex_Digit_Display hex_digit_display_42 (.value(mask32_3_out_2[7:4]));  // open: dp

  // Other names for the same wires on the sheet: Count[15:0] = out_9

  // Notes on the sheet:
  //   *
  //   写寄存器
  //   $
  //   W@
  //   M@
  //   写内存
  //   <=
  //   W级PC
  //   M级PC
  //   <=
endmodule

module hex2dec (
  input  [4:0] hex5,
  output [3:0] hi,
  output [3:0] lo
);

  wire [4:0] divider_1_out, divider_1_rem;

  // Probe on hex5
  Divider #(.width(5)) divider_1 (.a(hex5), .b(5'b01010), .out(divider_1_out), .rem(divider_1_rem));  // open: upper
  Bit_Extender #(.in_width(5), .out_width(4)) bit_extender_1 (.in(divider_1_out), .out(hi));
  Bit_Extender #(.in_width(5), .out_width(4)) bit_extender_2 (.in(divider_1_rem), .out(lo));
  // Probe on hi
  // Probe on lo

  // Notes on the sheet:
  //   十六进制转十进制电路
  //   将5bit-十六进制转化成2位十进制
endmodule

module mask5 (
  input  [4:0] in,
  input  en,
  output [4:0] out
);

  Multiplexer #(.width(5), .enable("false")) multiplexer_1 (.in1(in), .out(out), .sel(en));  // open: in0
endmodule

module mask32 (
  input  [31:0] in,
  input  en,
  output [31:0] out
);

  Multiplexer #(.width(32), .enable("false")) multiplexer_1 (.in1(in), .out(out), .sel(en));  // open: in0
endmodule
