// Logisim project mips.circ as structural Verilog: 19 circuits, main circuit main
module test (
);

  Controller controller_1 ();  // open: Code, UseRs, AluOp, AddrRs, TuseRs, CmpOp, NpcOp, UseRt, ExtOp, AddrRt, TuseRt, AluSrc1, RegW, AluSrc2, Tnew, WDst, MemW, WSrc, MSz, AddrRd, MExt, Imm16, Imm26, Shamt
  CMP cmp_1 ();  // open: Src1, CmpOp, Src2, Flag
  ALU alu_1 ();  // open: Src1, AluOp, Src2, Out
  PC pc_1 ();  // open: Br, reset, Jmp, Stall, NpcOp, Ra, Flag, PC, NPC
  GRF grf_1 ();  // open: RAddr1, RAddr2, reset, WE, WAddr, WData, RData1, RData2
  MemAddr memaddr_1 ();  // open: Addr, Scale, MemW, ByteEn, MAddr, Offset
  MemExt memext_1 ();  // open: MWord, Offset, Ext, Sz, MRead
  RegInit32 reginit32_1 ();  // open: D, reset, WE, Val, Q
  ForwardUnit forwardunit_1 ();  // open: W1, W2, A0, A1, A2, D0, D1, D2, NoFwd, Fwd1, D, Fwd2
  ForwardUnit forwardunit_2 ();  // open: W1, W2, A0, A1, A2, D0, D1, D2, NoFwd, Fwd1, D, Fwd2
  StallUnit stallunit_1 ();  // open: UseRs_D, UseRt_D, W_E, W_M, AddrRs_D, AddrRt_D, A_E, A_M, TuseRs_D, TuseRt_D, Tnew_E, Tnew_M, Stall
  DM dm_1 ();  // open: A, DIn, ByteEn, DOut, Reset
  F_D f_d_1 ();  // open: Reset, Stall, PC_I, Code_I, PC_O, Code_O
  D_E d_e_1 ();  // open: W_I, Reset, Clear, A_I, PC_I, D_I, Tnew_I, Code_I, AddrRs_I, AddrRt_I, DataRs_I, DataRt_I, AluOp_I, AluSrc1_I, AluSrc2_I, MemW_I, MExt_I, W_O, A_O, PC_O, D_O, Tnew_O, Code_O, AddrRs_O, AddrRt_O, DataRs_O, DataRt_O, AluOp_O, AluSrc1_O, AluSrc2_O, MemW_O, MSz_O, MExt_O, Imm32_I, Imm32_O, Shamt32_I, Shamt32_O, MSz_I, WSrc_I, WSrc_O
  E_M e_m_1 ();  // open: W_I, Reset, A_I, PC_I, D_I, Code_I, AddrRt_I, MemW_I, MSz_I, DataRt_I, MExt_I, AluOut_I, W_O, A_O, PC_O, D_O, Code_O, AddrRt_O, MemW_O, MSz_O, DataRt_O, MExt_O, AluOut_O, Tnew_I, Tnew_O, WSrc_I, WSrc_O
  M_W m_w_1 ();  // open: W_I, Reset, A_I, PC_I, D_I, Code_I, MRD_I, Off_I, MSz_I, MExt_I, W_O, A_O, PC_O, D_O, Code_O, MRD_O, Off_O, MSz_O, MExt_O, WSrc_I, WSrc_O
endmodule

module RegInit32 (
  input  [31:0] D,
  input  reset,
  input  WE,
  input  [31:0] Val,
  output [31:0] Q
);

  wire clk, init, nor_1_out, or_1_out;
  wire [31:0] multiplexer_1_out, register_1_q;

  Clock u_clk (.out(clk));
  Pull_Resistor pull_resistor_1 (.node(reset));
  Pull_Resistor pull_resistor_2 (.node(WE));
  Counter #(.width(1), .max('h1), .ongoal("stay")) counter_1 (
    .carry(init), .clk(clk), .clr(reset));  // open: load, D, count, Q
  Pull_Resistor pull_resistor_3 (.node(D));
  Pull_Resistor pull_resistor_4 (.node(Val));
  Multiplexer #(.width(32), .disabled(0), .enable("false")) multiplexer_1 (
    .in0(D), .in1(Val), .out(multiplexer_1_out), .sel(nor_1_out));
  nor nor_1 (nor_1_out, init, WE);
  Register #(.width(32)) register_1 (.D(multiplexer_1_out), .en(or_1_out), .Q(register_1_q), .clk(clk), .clr(reset));
  or or_1 (or_1_out, ~init, WE);  // OR_Gate
  Multiplexer #(.width(32), .disabled(0), .enable("false")) multiplexer_2 (
    .in0(Val), .in1(register_1_q), .out(Q), .sel(init));

  // Notes on the sheet:
  //   IO
  //   Init
  //   Reg
endmodule

module GRF (
  input  [4:0] RAddr1,
  input  [4:0] RAddr2,
  input  [4:0] WAddr,
  input  reset,
  input  WE,
  input  [31:0] WData,
  output [31:0] RData1,
  output [31:0] RData2
);

  wire and_1_out, and_2_out, clk, comparator_1_eq, comparator_2_eq, comparator_3_eq, comparator_4_eq, WE1,
       WE2, WE3, WE4, WE5, WE6, WE7, WE8, WE9, WE10, WE11, WE12, WE13, WE14, WE15, WE16, WE17, WE18, WE19,
       WE20, WE21, WE22, WE23, WE24, WE25, WE26, WE27, WE28, WE29, WE30, WE31;
  wire [31:0] R0, R1, R2, R3, R4, R5, R6, R7, R8, R9, R10, R11, R12, R13, R14, R15, R16, R17, R18, R19, R20,
       R21, R22, R23, R24, R25, R26, R27, R28, R29, R30, R31, RD1, RD2;

  Clock u_clk (.out(clk));
  Pull_Resistor pull_resistor_1 (.node(reset));
  Pull_Resistor pull_resistor_2 (.node(WE));
  Comparator #(.width(5), .mode("unsigned")) comparator_1 (
    .a(WAddr), .b(RAddr1), .eq(comparator_1_eq));  // open: gt, lt
  Comparator #(.width(5), .mode("unsigned")) comparator_2 (
    .a(WAddr), .b({5{1'b0}}), .eq(comparator_2_eq));  // open: gt, lt
  Comparator #(.width(5), .mode("unsigned")) comparator_3 (
    .a(WAddr), .b(RAddr2), .eq(comparator_3_eq));  // open: gt, lt
  Comparator #(.width(5), .mode("unsigned")) comparator_4 (
    .a(WAddr), .b({5{1'b0}}), .eq(comparator_4_eq));  // open: gt, lt
  Register #(.width(32)) u_r0 (.en(1'b0), .Q(R0), .clk(clk), .clr(reset));  // open: D
  Register #(.width(32)) u_r8 (.D(WData), .en(WE8), .Q(R8), .clk(clk), .clr(reset));
  Register #(.width(32)) u_r16 (.D(WData), .en(WE16), .Q(R16), .clk(clk), .clr(reset));
  Register #(.width(32)) u_r24 (.D(WData), .en(WE24), .Q(R24), .clk(clk), .clr(reset));
  Demultiplexer #(.select(5), .disabled(0), .enable("false")) demultiplexer_1 (
    .out1(WE1), .out2(WE2), .out3(WE3), .out4(WE4), .out5(WE5), .out6(WE6), .out7(WE7), .out8(WE8),
    .out9(WE9), .out10(WE10), .out11(WE11), .out12(WE12), .out13(WE13), .out14(WE14), .out15(WE15),
    .out16(WE16), .out17(WE17), .out18(WE18), .out19(WE19), .out20(WE20), .out21(WE21), .out22(WE22),
    .out23(WE23), .out24(WE24), .out25(WE25), .out26(WE26), .out27(WE27), .out28(WE28), .out29(WE29),
    .out30(WE30), .out31(WE31), .in(WE), .sel(WAddr));  // open: out0
  and and_1 (and_1_out, comparator_1_eq, WE, ~comparator_2_eq);  // AND_Gate
  and and_2 (and_2_out, comparator_3_eq, WE, ~comparator_4_eq);  // AND_Gate
  Pull_Resistor pull_resistor_3 (.node(RAddr1));
  Pull_Resistor pull_resistor_4 (.node(RAddr2));
  Pull_Resistor pull_resistor_5 (.node(WAddr));
  Pull_Resistor pull_resistor_6 (.node(WData));
  Multiplexer #(.width(32), .disabled(0), .enable("false")) multiplexer_1 (
    .in0(RD1), .in1(WData), .out(RData1), .sel(and_1_out));
  Multiplexer #(.width(32), .disabled(0), .enable("false")) multiplexer_2 (
    .in0(RD2), .in1(WData), .out(RData2), .sel(and_2_out));
  Register #(.width(32)) u_r1 (.D(WData), .en(WE1), .Q(R1), .clk(clk), .clr(reset));
  Register #(.width(32)) u_r9 (.D(WData), .en(WE9), .Q(R9), .clk(clk), .clr(reset));
  Register #(.width(32)) u_r17 (.D(WData), .en(WE17), .Q(R17), .clk(clk), .clr(reset));
  Register #(.width(32)) u_r25 (.D(WData), .en(WE25), .Q(R25), .clk(clk), .clr(reset));
  Register #(.width(32)) u_r2 (.D(WData), .en(WE2), .Q(R2), .clk(clk), .clr(reset));
  Register #(.width(32)) u_r10 (.D(WData), .en(WE10), .Q(R10), .clk(clk), .clr(reset));
  Register #(.width(32)) u_r18 (.D(WData), .en(WE18), .Q(R18), .clk(clk), .clr(reset));
  Register #(.width(32)) u_r26 (.D(WData), .en(WE26), .Q(R26), .clk(clk), .clr(reset));
  // Probe on RAddr1
  // Probe on RAddr2
  // Probe on WAddr
  // Probe on WData
  Register #(.width(32)) u_r3 (.D(WData), .en(WE3), .Q(R3), .clk(clk), .clr(reset));
  Register #(.width(32)) u_r11 (.D(WData), .en(WE11), .Q(R11), .clk(clk), .clr(reset));
  Register #(.width(32)) u_r19 (.D(WData), .en(WE19), .Q(R19), .clk(clk), .clr(reset));
  Register #(.width(32)) u_r27 (.D(WData), .en(WE27), .Q(R27), .clk(clk), .clr(reset));
  Multiplexer #(.select(5), .width(32), .disabled(0), .enable("false")) multiplexer_3 (
    .in0(R0), .in1(R1), .in2(R2), .in3(R3), .in4(R4), .in5(R5), .in6(R6), .in7(R7), .in8(R8), .in9(R9),
    .in10(R10), .in11(R11), .in12(R12), .in13(R13), .in14(R14), .in15(R15), .in16(R16), .in17(R17),
    .in18(R18), .in19(R19), .in20(R20), .in21(R21), .in22(R22), .in23(R23), .in24(R24), .in25(R25),
    .in26(R26), .in27(R27), .in28(R28), .in29(R29), .in30(R30), .in31(R31), .out(RD1), .sel(RAddr1));
  Register #(.width(32)) u_r4 (.D(WData), .en(WE4), .Q(R4), .clk(clk), .clr(reset));
  Register #(.width(32)) u_r12 (.D(WData), .en(WE12), .Q(R12), .clk(clk), .clr(reset));
  Register #(.width(32)) u_r20 (.D(WData), .en(WE20), .Q(R20), .clk(clk), .clr(reset));
  Register #(.width(32)) u_r28 (.D(WData), .en(WE28), .Q(R28), .clk(clk), .clr(reset));
  // Probe on R0
  // Probe on R1
  // Probe on R2
  // Probe on R3
  // Probe on R4
  // Probe on R5
  // Probe on R6
  // Probe on R7
  // Probe on R8
  // Probe on R9
  // Probe on R10
  // Probe on R11
  // Probe on R12
  // Probe on R13
  // Probe on R14
  // Probe on R15
  Register #(.width(32)) u_r5 (.D(WData), .en(WE5), .Q(R5), .clk(clk), .clr(reset));
  Register #(.width(32)) u_r13 (.D(WData), .en(WE13), .Q(R13), .clk(clk), .clr(reset));
  Register #(.width(32)) u_r21 (.D(WData), .en(WE21), .Q(R21), .clk(clk), .clr(reset));
  Register #(.width(32)) u_r29 (.D(WData), .en(WE29), .Q(R29), .clk(clk), .clr(reset));
  Multiplexer #(.select(5), .width(32), .disabled(0), .enable("false")) multiplexer_4 (
    .in0(R0), .in1(R1), .in2(R2), .in3(R3), .in4(R4), .in5(R5), .in6(R6), .in7(R7), .in8(R8), .in9(R9),
    .in10(R10), .in11(R11), .in12(R12), .in13(R13), .in14(R14), .in15(R15), .in16(R16), .in17(R17),
    .in18(R18), .in19(R19), .in20(R20), .in21(R21), .in22(R22), .in23(R23), .in24(R24), .in25(R25),
    .in26(R26), .in27(R27), .in28(R28), .in29(R29), .in30(R30), .in31(R31), .out(RD2), .sel(RAddr2));
  // Probe on R16
  // Probe on R17
  // Probe on R18
  // Probe on R19
  // Probe on R20
  // Probe on R21
  // Probe on R22
  // Probe on R23
  // Probe on R24
  // Probe on R25
  // Probe on R26
  // Probe on R27
  // Probe on R28
  // Probe on R29
  // Probe on R30
  // Probe on R31
  Register #(.width(32)) u_r6 (.D(WData), .en(WE6), .Q(R6), .clk(clk), .clr(reset));
  Register #(.width(32)) u_r14 (.D(WData), .en(WE14), .Q(R14), .clk(clk), .clr(reset));
  Register #(.width(32)) u_r22 (.D(WData), .en(WE22), .Q(R22), .clk(clk), .clr(reset));
  Register #(.width(32)) u_r30 (.D(WData), .en(WE30), .Q(R30), .clk(clk), .clr(reset));
  Register #(.width(32)) u_r7 (.D(WData), .en(WE7), .Q(R7), .clk(clk), .clr(reset));
  Register #(.width(32)) u_r15 (.D(WData), .en(WE15), .Q(R15), .clk(clk), .clr(reset));
  Register #(.width(32)) u_r23 (.D(WData), .en(WE23), .Q(R23), .clk(clk), .clr(reset));
  Register #(.width(32)) u_r31 (.D(WData), .en(WE31), .Q(R31), .clk(clk), .clr(reset));

  // Notes on the sheet:
  //   IO
  //   Control
  //   DataIn
  //   Forward
  //   DataOut
  //   Select
  //   Register
  //   Monitor
endmodule

module ALU (
  input  [31:0] Src1,
  input  [4:0] AluOp,
  input  [31:0] Src2,
  output [31:0] Out
);

  wire comparator_1_lt, comparator_2_lt;
  wire [4:0] bit_extender_1_out, bit_extender_2_out, bit_extender_3_out;
  wire [31:0] Addu, And, Nor, Or, Sll, Slt, Sltu, Sra, Srl, Subu, Xor;

  Pull_Resistor pull_resistor_1 (.node(AluOp));
  Adder #(.width(32)) adder_1 (.a(Src1), .b(Src2), .out(Addu));  // open: cin, cout
  Subtractor #(.width(32)) subtractor_1 (.a(Src1), .b(Src2), .out(Subu));  // open: bin, bout
  assign And = Src1 & Src2;  // AND_Gate and_1, 32 bits wide
  assign Or = Src1 | Src2;  // OR_Gate or_1, 32 bits wide
  assign Xor = Src1 ^ Src2;  // XOR_Gate xor_1, 32 bits wide
  assign Nor = ~(Src1 | Src2);  // NOR_Gate nor_1, 32 bits wide
  Pull_Resistor pull_resistor_2 (.node(Src1));
  Pull_Resistor pull_resistor_3 (.node(Src2));
  Comparator #(.width(32)) comparator_1 (.a(Src1), .b(Src2), .lt(comparator_1_lt));  // open: gt, eq
  Comparator #(.width(32), .mode("unsigned")) comparator_2 (.a(Src1), .b(Src2), .lt(comparator_2_lt));  // open: gt, eq
  Bit_Extender #(.in_width(32), .out_width(5)) bit_extender_1 (.in(Src1), .out(bit_extender_1_out));
  Bit_Extender #(.in_width(32), .out_width(5)) bit_extender_2 (.in(Src1), .out(bit_extender_2_out));
  Bit_Extender #(.in_width(32), .out_width(5)) bit_extender_3 (.in(Src1), .out(bit_extender_3_out));
  assign Slt = {{31{1'b0}}, comparator_1_lt};  // Bit_Extender bit_extender_4
  assign Sltu = {{31{1'b0}}, comparator_2_lt};  // Bit_Extender bit_extender_5
  Shifter #(.width(32)) shifter_1 (.in(Src2), .\dist (bit_extender_1_out), .out(Sll));
  Shifter #(.width(32), .shift("lr")) shifter_2 (.in(Src2), .\dist (bit_extender_2_out), .out(Srl));
  Shifter #(.width(32), .shift("ar")) shifter_3 (.in(Src2), .\dist (bit_extender_3_out), .out(Sra));
  // Probe on Src1
  // Probe on Src2
  // Probe on Out
  // Probe on AluOp
  Multiplexer #(.select(5), .width(32), .disabled(0), .enable("false")) multiplexer_1 (
    .in0({32{1'b0}}), .in1(Src1), .in2(Src2), .in3(Addu), .in4(Subu), .in5(And), .in6(Or), .in7(Xor),
    .in8(Nor), .in9(Slt), .in10(Sltu), .in11(Sll), .in12(Srl), .in13(Sra), .in31({32{1'b1}}), .out(Out),
    .sel(AluOp));  // open: in14, in15, in16, in17, in18, in19, in20, in21, in22, in23, in24, in25, in26, in27, in28, in29, in30
  Pull_Resistor pull_resistor_4 (.node(Out));

  // Notes on the sheet:
  //   Control
  //   DataIn
  //   Op
  //   DataOut
  //   Monitor
  //   Select
endmodule

module CMP (
  input  [31:0] Src1,
  input  [4:0] CmpOp,
  input  [31:0] Src2,
  output Flag
);

  wire Eq, Eqz, Ge, Gez, Gt, Gtz, Le, Lez, Lt, Ltz, Ne, Nez;

  Pull_Resistor pull_resistor_1 (.node(CmpOp));
  Pull_Resistor pull_resistor_2 (.node(Flag));
  Comparator #(.width(32)) comparator_1 (.a(Src1), .b(Src2), .gt(Gt), .eq(Eq), .lt(Lt));
  or or_1 (Ge, Gt, Eq);
  not not_1 (Ne, Eq);
  or or_2 (Le, Eq, Lt);
  Pull_Resistor pull_resistor_3 (.node(Src1));
  Pull_Resistor pull_resistor_4 (.node(Src2));
  Comparator #(.width(32)) comparator_2 (.a(Src1), .b({32{1'b0}}), .gt(Gtz), .eq(Eqz), .lt(Ltz));
  or or_3 (Gez, Gtz, Eqz);
  not not_2 (Nez, Eqz);
  or or_4 (Lez, Eqz, Ltz);
  // Probe on Src1
  // Probe on Src2
  // Probe on CmpOp
  LED led_1 (.in(Flag));
  Multiplexer #(.select(5), .disabled(0), .enable("false")) multiplexer_1 (
    .in0(1'b0), .in1(1'b1), .in2(Eq), .in3(Ne), .in4(Gtz), .in5(Ltz), .in6(Gez), .in7(Lez), .out(Flag),
    .sel(CmpOp));  // open: in8, in9, in10, in11, in12, in13, in14, in15, in16, in17, in18, in19, in20, in21, in22, in23, in24, in25, in26, in27, in28, in29, in30, in31

  // Notes on the sheet:
  //   Control
  //   Out
  //   Compare
  //   Data
  //   Monitor
  //   Select
endmodule

module PC (
  input  [15:0] Br,
  input  reset,
  input  [25:0] Jmp,
  input  Stall,
  input  [2:0] NpcOp,
  input  [31:0] Ra,
  input  Flag,
  output [31:0] PC,
  output [31:0] NPC
);

  wire clk, not_1_out;
  wire [31:0] bit_extender_1_out, brNPC, brTarget, rawNPC, shifter_1_out;

  Clock u_clk (.out(clk));
  Pull_Resistor pull_resistor_1 (.node(reset));
  Pull_Resistor pull_resistor_2 (.node(Stall));
  Pull_Resistor pull_resistor_3 (.node(NpcOp));
  Pull_Resistor pull_resistor_4 (.node(Flag));
  RegInit32 reginit32_1 (.D(NPC), .reset(reset), .WE(not_1_out), .Val(32'h3000), .Q(PC));
  not not_1 (not_1_out, Stall);
  Multiplexer #(.select(3), .width(32), .disabled(0), .enable("false")) multiplexer_1 (
    .in0(rawNPC), .in1(brNPC), .in2({PC[31:28], Jmp, 2'b00}), .in3(Ra), .out(NPC), .sel(NpcOp));  // open: in4, in5, in6, in7
  Pull_Resistor pull_resistor_5 (.node(Br));
  Pull_Resistor pull_resistor_6 (.node(Jmp));
  Pull_Resistor pull_resistor_7 (.node(Ra));
  Adder #(.width(32)) adder_1 (.a(PC), .b(32'h4), .out(rawNPC));  // open: cin, cout
  assign bit_extender_1_out = {{16{Br[15]}}, Br};  // Bit_Extender bit_extender_1
  Multiplexer #(.width(32), .disabled(0), .enable("false")) multiplexer_2 (
    .in0(rawNPC), .in1(brTarget), .out(brNPC), .sel(Flag));
  Shifter #(.width(32)) shifter_1 (.in(bit_extender_1_out), .\dist (5'b00010), .out(shifter_1_out));
  Adder #(.width(32)) adder_2 (.a(shifter_1_out), .b(PC), .out(brTarget));  // open: cin, cout

  // Other names for the same wires on the sheet: BrImm[15:0] = Br; JmpImm[25:0] = Jmp;
  //   jmpNPC[31:2] = {PC[31:28], Jmp}

  // Notes on the sheet:
  //   Control
  //   PC
  //   Select
  //   Input
  //   Calc-NPC
  //   State
endmodule

module EXT (
  input  [15:0] In,
  input  [1:0] ExtOp,
  output [31:0] out_3
);

  wire [31:0] bit_extender_1_out, bit_extender_2_out, bit_extender_3_out, shifter_1_out;

  Pull_Resistor pull_resistor_1 (.node(ExtOp));
  assign bit_extender_1_out = {{16{1'b0}}, In};  // Bit_Extender bit_extender_1
  assign bit_extender_2_out = {{16{In[15]}}, In};  // Bit_Extender bit_extender_2
  assign bit_extender_3_out = {{16{1'b0}}, In};  // Bit_Extender bit_extender_3
  Pull_Resistor pull_resistor_2 (.node(In));
  Shifter #(.width(32)) shifter_1 (.in(bit_extender_3_out), .\dist (5'b10000), .out(shifter_1_out));
  Multiplexer #(.select(2), .width(32), .disabled(0), .enable("false")) multiplexer_1 (
    .in0(bit_extender_1_out), .in1(bit_extender_2_out), .in2(shifter_1_out), .out(out_3), .sel(ExtOp));  // open: in3

  // Other names for the same wires on the sheet: Out[31:0] = out_3

  // Notes on the sheet:
  //   Input
  //   Output
  //   EXT
endmodule

module MemAddr (
  input  [31:0] Addr,
  input  [1:0] Scale,
  input  MemW,
  output [3:0] ByteEn,
  output [11:0] MAddr,
  output [1:0] Offset
);

  wire [1:0] and_1_out;
  wire [3:0] shifter_1_out, shifter_2_out;

  Pull_Resistor pull_resistor_1 (.node(Addr));
  Pull_Resistor pull_resistor_2 (.node(Scale));
  Pull_Resistor pull_resistor_3 (.node(MemW));
  Shifter #(.width(4)) shifter_1 (.in(4'b0001), .\dist (Addr[1:0]), .out(shifter_1_out));
  Shifter #(.width(4)) shifter_2 (.in(4'b0011), .\dist (and_1_out), .out(shifter_2_out));
  assign and_1_out = Addr[1:0] & 2'b10;  // AND_Gate and_1, 2 bits wide
  Multiplexer #(.select(2), .width(4), .disabled(0)) multiplexer_1 (
    .in0(4'b0000), .in1(shifter_1_out), .in2(shifter_2_out), .in3(4'b1111), .out(ByteEn), .sel(Scale),
    .en(MemW));

  assign MAddr = Addr[13:2];
  assign Offset = Addr[1:0];

  // Notes on the sheet:
  //   Split
  //   Input
  //   Output
  //   ByteEn
endmodule

module MemExt (
  input  [31:0] MWord,
  input  [1:0] Offset,
  input  Ext,
  input  [1:0] Sz,
  output [31:0] MRead
);

  wire [7:0] multiplexer_1_out;
  wire [15:0] multiplexer_2_out;
  wire [31:0] bit_extender_1_out, bit_extender_2_out, bit_extender_3_out, bit_extender_4_out,
       multiplexer_3_out, multiplexer_4_out;

  Pull_Resistor pull_resistor_1 (.node(Offset));
  Pull_Resistor pull_resistor_2 (.node(MWord));
  Pull_Resistor pull_resistor_3 (.node(Ext));
  Multiplexer #(.select(2), .width(8), .disabled(0), .enable("false")) multiplexer_1 (
    .in0(MWord[7:0]), .in1(MWord[15:8]), .in2(MWord[23:16]), .in3(MWord[31:24]), .out(multiplexer_1_out),
    .sel(Offset));
  Multiplexer #(.width(16), .disabled(0), .enable("false")) multiplexer_2 (
    .in0(MWord[15:0]), .in1(MWord[31:16]), .out(multiplexer_2_out), .sel(Offset[1]));
  assign bit_extender_1_out = {{24{1'b0}}, multiplexer_1_out};  // Bit_Extender bit_extender_1
  Multiplexer #(.width(32), .disabled(0), .enable("false")) multiplexer_3 (
    .in0(bit_extender_1_out), .in1(bit_extender_2_out), .out(multiplexer_3_out), .sel(Ext));
  assign bit_extender_2_out = {{24{multiplexer_1_out[7]}}, multiplexer_1_out};  // Bit_Extender bit_extender_2
  assign bit_extender_3_out = {{16{1'b0}}, multiplexer_2_out};  // Bit_Extender bit_extender_3
  Multiplexer #(.width(32), .disabled(0), .enable("false")) multiplexer_4 (
    .in0(bit_extender_3_out), .in1(bit_extender_4_out), .out(multiplexer_4_out), .sel(Ext));
  assign bit_extender_4_out = {{16{multiplexer_2_out[15]}}, multiplexer_2_out};  // Bit_Extender bit_extender_4
  Pull_Resistor pull_resistor_4 (.node(Sz));
  Multiplexer #(.select(2), .width(32), .disabled(0), .enable("false")) multiplexer_5 (
    .in0({32{1'b0}}), .in1(multiplexer_3_out), .in2(multiplexer_4_out), .in3(MWord), .out(MRead), .sel(Sz));

  // Notes on the sheet:
  //   Extract-Extend
  //   Data
  //   Ctrl
endmodule

module Controller (
  input  [31:0] Code,
  output UseRs,
  output [4:0] AluOp,
  output [4:0] AddrRs,
  output [2:0] TuseRs,
  output [4:0] CmpOp,
  output [2:0] NpcOp,
  output UseRt,
  output [1:0] ExtOp,
  output [4:0] AddrRt,
  output [2:0] TuseRt,
  output AluSrc1,
  output [15:0] Imm16,
  output RegW,
  output AluSrc2,
  output [2:0] Tnew,
  output [25:0] Imm26,
  output [2:0] WDst,
  output MemW,
  output [2:0] WSrc,
  output [1:0] MSz,
  output [4:0] Shamt,
  output [4:0] AddrRd,
  output MExt
);

  wire _b, _b1, _b2, _i_alu, _i_arith, _i_logic, _mem, _memr, _r_alu, _r_sh2, add, addi, addiu, addu, \and ,
       andi, beq, bgez, bgtz, blez, bltz, bne, comparator_1_eq, comparator_2_eq, comparator_3_eq,
       comparator_4_eq, comparator_14_eq, comparator_15_eq, comparator_16_eq, comparator_17_eq,
       comparator_22_eq, comparator_23_eq, comparator_24_eq, comparator_25_eq, comparator_30_eq,
       comparator_31_eq, comparator_32_eq, comparator_33_eq, comparator_38_eq, comparator_39_eq,
       comparator_40_eq, comparator_41_eq, comparator_42_eq, j, jal, jalr, jr, lb, lbu, lh, lhu, lui, lw,
       \nor , not_1_out, \or , or_3_out, or_4_out, or_5_out, or_6_out, or_12_out, or_13_out, or_14_out,
       or_15_out, or_16_out, or_17_out, or_18_out, or_19_out, or_20_out, or_25_out, or_26_out, or_27_out,
       or_31_out, or_32_out, or_33_out, or_34_out, or_35_out, or_36_out, or_37_out, or_38_out, or_39_out,
       or_42_out, or_44_out, ori, RInstr, sb, sh, sll, sllv, slt, slti, sltiu, sltu, sra, srav, srl, srlv,
       sub, subu, sw, \xor , xori;

  Comparator #(.width(6), .mode("unsigned")) comparator_1 (
    .a(Code[5:0]), .b(6'b100000), .eq(comparator_1_eq));  // open: gt, lt
  Comparator #(.width(6), .mode("unsigned")) comparator_2 (
    .a(Code[5:0]), .b(6'b100001), .eq(comparator_2_eq));  // open: gt, lt
  Comparator #(.width(6), .mode("unsigned")) comparator_3 (
    .a(Code[5:0]), .b(6'b100010), .eq(comparator_3_eq));  // open: gt, lt
  Comparator #(.width(6), .mode("unsigned")) comparator_4 (
    .a(Code[5:0]), .b(6'b100011), .eq(comparator_4_eq));  // open: gt, lt
  or or_1 (MExt, lb, sb);
  Pull_Resistor pull_resistor_1 (.node(Code));
  // Probe on Code
  and and_1 (add, RInstr, comparator_1_eq);
  and and_2 (addu, RInstr, comparator_2_eq);
  and and_3 (sub, RInstr, comparator_3_eq);
  and and_4 (subu, RInstr, comparator_4_eq);
  Comparator #(.width(6), .mode("unsigned")) comparator_5 (.a(Code[31:26]), .b(6'b001000), .eq(addi));  // open: gt, lt
  Comparator #(.width(6), .mode("unsigned")) comparator_6 (.a(Code[31:26]), .b(6'b001001), .eq(addiu));  // open: gt, lt
  Comparator #(.width(6), .mode("unsigned")) comparator_7 (.a(Code[31:26]), .b(6'b001100), .eq(andi));  // open: gt, lt
  Comparator #(.width(6), .mode("unsigned")) comparator_8 (.a(Code[31:26]), .b(6'b001101), .eq(ori));  // open: gt, lt
  or or_2 (_r_alu, slt, add, \and , addu, \or , sub, \xor , subu, \nor , sltu);
  or or_3 (or_3_out, _b, or_4_out);
  or or_4 (or_4_out, jr, jalr);
  or or_5 (or_5_out, _i_alu, _r_alu, _mem, _r_sh2);
  or or_6 (or_6_out, _r_alu, _r_sh2, AluSrc1);
  or or_7 (AluSrc2, _i_alu, _mem);
  Comparator #(.width(6), .mode("unsigned")) comparator_9 (
    .a(Code[31:26]), .b({6{1'b0}}), .eq(RInstr));  // open: gt, lt
  or or_8 (UseRs, or_3_out, or_5_out);
  Pull_Resistor #(.pull(1)) pull_resistor_2 (.node(TuseRs));
  Priority_Encoder #(.disabled(0)) priority_encoder_1 (
    .in0(or_3_out), .in1(or_5_out), .out(TuseRs));  // open: in2, in3, in4, in5, in6, in7, en_in, gs, en_out
  or or_9 (UseRt, _b2, or_6_out, MemW);
  Priority_Encoder #(.disabled(0)) priority_encoder_2 (
    .in0(_b2), .in1(or_6_out), .in2(MemW), .out(TuseRt));  // open: in3, in4, in5, in6, in7, en_in, gs, en_out
  Pull_Resistor #(.pull(1)) pull_resistor_3 (.node(TuseRt));
  Comparator #(.width(6), .mode("unsigned")) comparator_10 (.a(Code[31:26]), .b(6'b001110), .eq(xori));  // open: gt, lt
  Comparator #(.width(6), .mode("unsigned")) comparator_11 (.a(Code[31:26]), .b(6'b001111), .eq(lui));  // open: gt, lt
  Comparator #(.width(6), .mode("unsigned")) comparator_12 (.a(Code[31:26]), .b(6'b001010), .eq(slti));  // open: gt, lt
  Comparator #(.width(6), .mode("unsigned")) comparator_13 (
    .a(Code[31:26]), .b(6'b001011), .eq(sltiu));  // open: gt, lt
  Comparator #(.width(6), .mode("unsigned")) comparator_14 (
    .a(Code[5:0]), .b(6'b100100), .eq(comparator_14_eq));  // open: gt, lt
  Comparator #(.width(6), .mode("unsigned")) comparator_15 (
    .a(Code[5:0]), .b(6'b100101), .eq(comparator_15_eq));  // open: gt, lt
  Comparator #(.width(6), .mode("unsigned")) comparator_16 (
    .a(Code[5:0]), .b(6'b100110), .eq(comparator_16_eq));  // open: gt, lt
  Comparator #(.width(6), .mode("unsigned")) comparator_17 (
    .a(Code[5:0]), .b(6'b100111), .eq(comparator_17_eq));  // open: gt, lt
  or or_10 (_r_sh2, sllv, srlv, srav);
  or or_11 (AluSrc1, sll, srl, sra);
  // Probe on Code[25:21]
  // Probe on TuseRs
  // Probe on Code[20:16]
  // Probe on TuseRt
  // Probe on Tnew
  // Probe on WDst
  // Probe on WSrc
  // Probe on Code[15:11]
  and and_5 (\and , RInstr, comparator_14_eq);
  and and_6 (\or , RInstr, comparator_15_eq);
  and and_7 (\xor , RInstr, comparator_16_eq);
  and and_8 (\nor , RInstr, comparator_17_eq);
  Comparator #(.width(6), .mode("unsigned")) comparator_18 (.a(Code[31:26]), .b(6'b100011), .eq(lw));  // open: gt, lt
  Comparator #(.width(6), .mode("unsigned")) comparator_19 (.a(Code[31:26]), .b(6'b101011), .eq(sw));  // open: gt, lt
  Comparator #(.width(6), .mode("unsigned")) comparator_20 (.a(Code[31:26]), .b(6'b100000), .eq(lb));  // open: gt, lt
  Comparator #(.width(6), .mode("unsigned")) comparator_21 (.a(Code[31:26]), .b(6'b100100), .eq(lbu));  // open: gt, lt
  or or_12 (or_12_out, lui, jalr, jal);
  not not_1 (not_1_out, RegW);
  or or_13 (or_13_out, _r_alu, _r_sh2, AluSrc1, _i_alu);
  or or_14 (or_14_out, _r_alu, _r_sh2, AluSrc1, jalr);
  or or_15 (or_15_out, _memr, lui, _i_alu);
  or or_16 (or_16_out, jalr, jal);
  or or_17 (or_17_out, _r_alu, _r_sh2, AluSrc1, _i_alu);
  or or_18 (or_18_out, lb, lbu, sb);
  or or_19 (or_19_out, lh, lhu, sh);
  or or_20 (or_20_out, lw, sw);
  Priority_Encoder #(.disabled(0)) priority_encoder_3 (
    .in0(not_1_out), .in1(or_12_out), .in2(or_13_out), .in3(_memr), .out(Tnew));  // open: in4, in5, in6, in7, en_in, gs, en_out
  Pull_Resistor pull_resistor_4 (.node(Tnew));
  or or_21 (RegW, or_14_out, or_15_out, jal);
  Pull_Resistor pull_resistor_5 (.node(WDst));
  Priority_Encoder #(.disabled(0)) priority_encoder_4 (
    .in0(or_14_out), .in1(or_15_out), .in2(jal), .out(WDst));  // open: in3, in4, in5, in6, in7, en_in, gs, en_out
  Priority_Encoder #(.disabled(0)) priority_encoder_5 (
    .in0(or_16_out), .in1(lui), .in2(or_17_out), .in3(_memr), .out(WSrc));  // open: in4, in5, in6, in7, en_in, gs, en_out
  Pull_Resistor pull_resistor_6 (.node(WSrc));
  Pull_Resistor pull_resistor_7 (.node(MSz));
  Priority_Encoder #(.select(2), .disabled(0)) priority_encoder_6 (
    .in1(or_18_out), .in2(or_19_out), .in3(or_20_out), .out(MSz));  // open: in0, gs, en_out, en_in
  Comparator #(.width(6), .mode("unsigned")) comparator_22 (
    .a(Code[5:0]), .b({6{1'b0}}), .eq(comparator_22_eq));  // open: gt, lt
  Comparator #(.width(6), .mode("unsigned")) comparator_23 (
    .a(Code[5:0]), .b(6'b000010), .eq(comparator_23_eq));  // open: gt, lt
  Comparator #(.width(6), .mode("unsigned")) comparator_24 (
    .a(Code[5:0]), .b(6'b000011), .eq(comparator_24_eq));  // open: gt, lt
  Comparator #(.width(6), .mode("unsigned")) comparator_25 (
    .a(Code[5:0]), .b(6'b101010), .eq(comparator_25_eq));  // open: gt, lt
  Comparator #(.width(6), .mode("unsigned")) comparator_26 (.a(Code[31:26]), .b(6'b100001), .eq(lh));  // open: gt, lt
  Comparator #(.width(6), .mode("unsigned")) comparator_27 (.a(Code[31:26]), .b(6'b100101), .eq(lhu));  // open: gt, lt
  Comparator #(.width(6), .mode("unsigned")) comparator_28 (.a(Code[31:26]), .b(6'b101000), .eq(sb));  // open: gt, lt
  Comparator #(.width(6), .mode("unsigned")) comparator_29 (.a(Code[31:26]), .b(6'b101001), .eq(sh));  // open: gt, lt
  or or_22 (_i_arith, addiu, addi, slti, sltiu);
  or or_23 (_i_alu, _i_arith, _i_logic);
  or or_24 (_i_logic, xori, andi, ori);
  // Probe on AluOp
  // Probe on CmpOp
  // Probe on NpcOp
  // Probe on ExtOp
  and and_9 (sll, RInstr, comparator_22_eq);
  and and_10 (srl, RInstr, comparator_23_eq);
  and and_11 (sra, RInstr, comparator_24_eq);
  and and_12 (slt, RInstr, comparator_25_eq);
  or or_25 (or_25_out, j, jal);
  or or_26 (or_26_out, jr, jalr);
  or or_27 (or_27_out, _i_arith, _mem);
  Comparator #(.width(6), .mode("unsigned")) comparator_30 (
    .a(Code[5:0]), .b(6'b000100), .eq(comparator_30_eq));  // open: gt, lt
  Comparator #(.width(6), .mode("unsigned")) comparator_31 (
    .a(Code[5:0]), .b(6'b000110), .eq(comparator_31_eq));  // open: gt, lt
  Comparator #(.width(6), .mode("unsigned")) comparator_32 (
    .a(Code[5:0]), .b(6'b000111), .eq(comparator_32_eq));  // open: gt, lt
  Comparator #(.width(6), .mode("unsigned")) comparator_33 (
    .a(Code[5:0]), .b(6'b101011), .eq(comparator_33_eq));  // open: gt, lt
  Comparator #(.width(6), .mode("unsigned")) comparator_34 (.a(Code[31:26]), .b(6'b000100), .eq(beq));  // open: gt, lt
  Comparator #(.width(6), .mode("unsigned")) comparator_35 (.a(Code[31:26]), .b(6'b000101), .eq(bne));  // open: gt, lt
  Comparator #(.width(6), .mode("unsigned")) comparator_36 (.a(Code[31:26]), .b(6'b000111), .eq(bgtz));  // open: gt, lt
  Comparator #(.width(6), .mode("unsigned")) comparator_37 (.a(Code[31:26]), .b(6'b000110), .eq(blez));  // open: gt, lt
  or or_28 (_memr, lw, lhu, lh, lbu, lb);
  or or_29 (_mem, _memr, MemW);
  or or_30 (MemW, sw, sb, sh);
  Priority_Encoder #(.select(5), .disabled(0)) priority_encoder_7 (
    .in2(beq), .in3(bne), .in4(bgtz), .in5(bltz), .in6(bgez), .in7(blez), .out(CmpOp));  // open: in0, in1, in8, in9, in10, in11, in12, in13, in14, in15, in16, in17, in18, in19, in20, in21, in22, in23, in24, in25, in26, in27, in28, in29, in30, in31, gs, en_out, en_in
  Pull_Resistor pull_resistor_8 (.node(CmpOp));
  Pull_Resistor pull_resistor_9 (.node(NpcOp));
  Priority_Encoder #(.disabled(0)) priority_encoder_8 (
    .in1(_b), .in2(or_25_out), .in3(or_26_out), .out(NpcOp));  // open: in0, in4, in5, in6, in7, en_in, gs, en_out
  Pull_Resistor pull_resistor_10 (.node(ExtOp));
  Priority_Encoder #(.select(2), .disabled(0)) priority_encoder_9 (
    .in1(or_27_out), .in2(lui), .out(ExtOp));  // open: in0, in3, gs, en_out, en_in
  and and_13 (sllv, RInstr, comparator_30_eq);
  and and_14 (srlv, RInstr, comparator_31_eq);
  and and_15 (srav, RInstr, comparator_32_eq);
  and and_16 (sltu, RInstr, comparator_33_eq);
  Comparator #(.width(6), .mode("unsigned")) comparator_38 (
    .a(Code[31:26]), .b(6'b000001), .eq(comparator_38_eq));  // open: gt, lt
  and and_17 (bgez, comparator_38_eq, comparator_39_eq);
  Comparator #(.width(5), .mode("unsigned")) comparator_39 (
    .a(Code[20:16]), .b(5'b00001), .eq(comparator_39_eq));  // open: gt, lt
  and and_18 (bltz, comparator_38_eq, comparator_40_eq);
  Comparator #(.width(5), .mode("unsigned")) comparator_40 (
    .a(Code[20:16]), .b({5{1'b0}}), .eq(comparator_40_eq));  // open: gt, lt
  or or_31 (or_31_out, sub, subu);
  or or_32 (or_32_out, \and , andi);
  or or_33 (or_33_out, \or , ori);
  or or_34 (or_34_out, \xor , xori);
  or or_35 (or_35_out, slt, slti);
  or or_36 (or_36_out, sltu, sltiu);
  or or_37 (or_37_out, sll, sllv);
  or or_38 (or_38_out, srl, srlv);
  or or_39 (or_39_out, sra, srav);
  or or_40 (_b2, beq, bne);
  or or_41 (_b1, bgez, bltz, blez, bgtz);
  or or_42 (or_42_out, add, addi, addu, addiu);
  and and_19 (jr, RInstr, comparator_41_eq);
  Comparator #(.width(6), .mode("unsigned")) comparator_41 (
    .a(Code[5:0]), .b(6'b001000), .eq(comparator_41_eq));  // open: gt, lt
  and and_20 (jalr, RInstr, comparator_42_eq);
  Comparator #(.width(6), .mode("unsigned")) comparator_42 (
    .a(Code[5:0]), .b(6'b001001), .eq(comparator_42_eq));  // open: gt, lt
  or or_43 (_b, _b2, _b1);
  or or_44 (or_44_out, or_42_out, _mem);
  Priority_Encoder #(.select(5), .disabled(0)) priority_encoder_10 (
    .in3(or_44_out), .in4(or_31_out), .in5(or_32_out), .in6(or_33_out), .in7(or_34_out), .in8(\nor ),
    .in9(or_35_out), .in10(or_36_out), .in11(or_37_out), .in12(or_38_out), .in13(or_39_out), .out(AluOp));  // open: in0, in1, in2, in14, in15, in16, in17, in18, in19, in20, in21, in22, in23, in24, in25, in26, in27, in28, in29, in30, in31, gs, en_out, en_in
  Comparator #(.width(6), .mode("unsigned")) comparator_43 (.a(Code[31:26]), .b(6'b000010), .eq(j));  // open: gt, lt
  Comparator #(.width(6), .mode("unsigned")) comparator_44 (.a(Code[31:26]), .b(6'b000011), .eq(jal));  // open: gt, lt
  Pull_Resistor pull_resistor_11 (.node(AluOp));

  assign AddrRd = Code[15:11];
  assign AddrRs = Code[25:21];
  assign AddrRt = Code[20:16];
  assign Imm16 = Code[15:0];
  assign Imm26 = Code[25:0];
  assign Shamt = Code[10:6];

  // Other names for the same wires on the sheet: _memw = MemW; MemWrite = MemW; _r_sh1 = AluSrc1;
  //   Funct[5:0] = Code[5:0]; Opcode[5:0] = Code[31:26]; MemExt = MExt; MemSz[1:0] = MSz; RegWrite = RegW

  // Notes on the sheet:
  //   Instruction
  //   Immediate
  //   ALU
  //   ALU
  //   RegUse1
  //   RegUse2
  //   RegWrite
  //   I-Type
  //   Signals
  //   Mem
  //   Operate
  //   Datapath
  //   Memory
  //   Instr-Parse
  //   R-Type
  //   Control-Signal Generate
  //   ALU-Shift
  //   Branch
  //   Jump
  //   J-Type
  //   Jump
  //   Instr Group
endmodule

module ForwardUnit (
  input  W1,
  input  W2,
  input  [4:0] A0,
  input  [4:0] A1,
  input  [4:0] A2,
  input  [31:0] D0,
  input  [31:0] D1,
  input  [31:0] D2,
  output NoFwd,
  output Fwd1,
  output [31:0] D,
  output Fwd2
);

  wire comparator_1_eq, comparator_2_eq, comparator_3_eq, comparator_4_eq, decoder_1_out2, decoder_1_out3,
       fwd1_t, fwd2_t;
  wire [31:0] multiplexer_1_out;

  Pull_Resistor pull_resistor_1 (.node(A0));
  Comparator #(.width(5), .mode("unsigned")) comparator_1 (.a(A1), .b(A0), .eq(comparator_1_eq));  // open: gt, lt
  Comparator #(.width(5), .mode("unsigned")) comparator_2 (
    .a(A1), .b({5{1'b0}}), .eq(comparator_2_eq));  // open: gt, lt
  Comparator #(.width(5), .mode("unsigned")) comparator_3 (.a(A2), .b(A0), .eq(comparator_3_eq));  // open: gt, lt
  Comparator #(.width(5), .mode("unsigned")) comparator_4 (
    .a(A2), .b({5{1'b0}}), .eq(comparator_4_eq));  // open: gt, lt
  and and_1 (fwd1_t, comparator_1_eq, W1, ~comparator_2_eq);  // AND_Gate
  and and_2 (fwd2_t, comparator_3_eq, W2, ~comparator_4_eq);  // AND_Gate
  Pull_Resistor pull_resistor_2 (.node(W1));
  Pull_Resistor pull_resistor_3 (.node(A1));
  Pull_Resistor pull_resistor_4 (.node(D1));
  Pull_Resistor pull_resistor_5 (.node(W2));
  Pull_Resistor pull_resistor_6 (.node(A2));
  Pull_Resistor pull_resistor_7 (.node(D2));
  Multiplexer #(.width(32), .disabled(0), .enable("false")) multiplexer_1 (
    .in0(D0), .in1(D2), .out(multiplexer_1_out), .sel(fwd2_t));
  Multiplexer #(.width(32), .disabled(0), .enable("false")) multiplexer_2 (
    .in0(multiplexer_1_out), .in1(D1), .out(D), .sel(fwd1_t));
  or or_1 (Fwd1, decoder_1_out2, decoder_1_out3);
  Decoder #(.select(2), .disabled(0), .enable("false")) decoder_1 (
    .out0(NoFwd), .out1(Fwd2), .out2(decoder_1_out2), .out3(decoder_1_out3), .sel({fwd1_t, fwd2_t}));
  // Probe on A0
  // Probe on A1
  // Probe on A2
  // Probe on D0
  // Probe on D1
  // Probe on D2
  // Probe on D

  // Notes on the sheet:
  //   IO
  //   In0(Read)
  //   Detect
  //   In1
  //   In2
  //   Select
  //   Out
  //   Monitor
  //   Signal
endmodule

module StallUnit (
  input  UseRs_D,
  input  UseRt_D,
  input  W_E,
  input  W_M,
  input  [4:0] AddrRs_D,
  input  [4:0] AddrRt_D,
  input  [4:0] A_E,
  input  [4:0] A_M,
  input  [2:0] TuseRs_D,
  input  [2:0] TuseRt_D,
  input  [2:0] Tnew_E,
  input  [2:0] Tnew_M,
  output Stall
);

  wire and_3_out, and_4_out, and_7_out, and_8_out, comparator_1_eq, comparator_2_eq, comparator_3_eq,
       comparator_4_gt, comparator_5_eq, comparator_6_gt, comparator_7_eq, comparator_8_gt, comparator_9_eq,
       comparator_10_gt, Rs_E, Rs_M, Rt_E, Rt_M, ValidRs, ValidRt;

  Pull_Resistor pull_resistor_1 (.node(UseRs_D));
  Pull_Resistor pull_resistor_2 (.node(AddrRs_D));
  Pull_Resistor pull_resistor_3 (.node(TuseRs_D));
  Comparator #(.width(5), .mode("unsigned")) comparator_1 (
    .a(AddrRs_D), .b({5{1'b0}}), .eq(comparator_1_eq));  // open: gt, lt
  Comparator #(.width(5), .mode("unsigned")) comparator_2 (
    .a(AddrRt_D), .b({5{1'b0}}), .eq(comparator_2_eq));  // open: gt, lt
  or or_1 (Stall, Rs_E, Rt_E, Rs_M, Rt_M);
  and and_1 (ValidRs, UseRs_D, ~comparator_1_eq);  // AND_Gate
  and and_2 (ValidRt, UseRt_D, ~comparator_2_eq);  // AND_Gate
  Pull_Resistor pull_resistor_4 (.node(UseRt_D));
  Pull_Resistor pull_resistor_5 (.node(AddrRt_D));
  Pull_Resistor pull_resistor_6 (.node(TuseRt_D));
  Comparator #(.width(5), .mode("unsigned")) comparator_3 (
    .a(A_E), .b(AddrRs_D), .eq(comparator_3_eq));  // open: gt, lt
  Comparator #(.width(3), .mode("unsigned")) comparator_4 (
    .a(Tnew_E), .b(TuseRs_D), .gt(comparator_4_gt));  // open: eq, lt
  Comparator #(.width(5), .mode("unsigned")) comparator_5 (
    .a(A_E), .b(AddrRt_D), .eq(comparator_5_eq));  // open: gt, lt
  Comparator #(.width(3), .mode("unsigned")) comparator_6 (
    .a(Tnew_E), .b(TuseRt_D), .gt(comparator_6_gt));  // open: eq, lt
  and and_3 (and_3_out, comparator_3_eq, W_E, comparator_4_gt);
  and and_4 (and_4_out, comparator_5_eq, W_E, comparator_6_gt);
  and and_5 (Rs_E, and_3_out, ValidRs);
  and and_6 (Rt_E, and_4_out, ValidRt);
  Comparator #(.width(5), .mode("unsigned")) comparator_7 (
    .a(A_M), .b(AddrRs_D), .eq(comparator_7_eq));  // open: gt, lt
  and and_7 (and_7_out, comparator_7_eq, W_M, comparator_8_gt);
  Comparator #(.width(3), .mode("unsigned")) comparator_8 (
    .a(Tnew_M), .b(TuseRs_D), .gt(comparator_8_gt));  // open: eq, lt
  Comparator #(.width(5), .mode("unsigned")) comparator_9 (
    .a(A_M), .b(AddrRt_D), .eq(comparator_9_eq));  // open: gt, lt
  and and_8 (and_8_out, comparator_9_eq, W_M, comparator_10_gt);
  Comparator #(.width(3), .mode("unsigned")) comparator_10 (
    .a(Tnew_M), .b(TuseRt_D), .gt(comparator_10_gt));  // open: eq, lt
  and and_9 (Rs_M, and_7_out, ValidRs);
  and and_10 (Rt_M, and_8_out, ValidRt);

  // Notes on the sheet:
  //   UseRs_D
  //   UseRt_D
  //   New_E
  //   New_M
  //   Stall_D
endmodule

module DM (
  input  [11:0] A,
  input  Reset,
  input  [31:0] DIn,
  input  [3:0] ByteEn,
  output [31:0] DOut
);

  wire Clk_out, WE;
  wire [31:0] DW;

  Pull_Resistor pull_resistor_1 (.node(A));
  Pull_Resistor pull_resistor_2 (.node(DIn));
  Pull_Resistor pull_resistor_3 (.node(ByteEn));
  or or_1 (WE, ByteEn[0], ByteEn[1], ByteEn[2], ByteEn[3]);
  Clock Clk (.out(Clk_out));
  RAM #(.addrWidth(12), .dataWidth(32), .bus("separate")) ram_1 (
    .addr(A), .din(DW), .data(DOut), .str(WE), .sel(1'b1), .clk(Clk_out), .ld(1'b1), .clr(Reset));
  // Probe on DW
  Multiplexer #(.width(8), .disabled(0), .enable("false")) multiplexer_1 (
    .in0(DOut[7:0]), .in1(DIn[7:0]), .out(DW[7:0]), .sel(ByteEn[0]));
  Multiplexer #(.width(8), .disabled(0), .enable("false")) multiplexer_2 (
    .in0(DOut[15:8]), .in1(DIn[15:8]), .out(DW[15:8]), .sel(ByteEn[1]));
  Multiplexer #(.width(8), .disabled(0), .enable("false")) multiplexer_3 (
    .in0(DOut[23:16]), .in1(DIn[23:16]), .out(DW[23:16]), .sel(ByteEn[2]));
  Multiplexer #(.width(8), .disabled(0), .enable("false")) multiplexer_4 (
    .in0(DOut[31:24]), .in1(DIn[31:24]), .out(DW[31:24]), .sel(ByteEn[3]));

  // Other names for the same wires on the sheet: DR[31:0] = DOut

  // Notes on the sheet:
  //   Memory
  //   ByteWrite
endmodule

module F_D (
  input  Reset,
  input  Stall,
  input  [31:0] PC_I,
  input  [31:0] Code_I,
  output [31:0] PC_O,
  output [31:0] Code_O
);

  wire clock_1_out, not_1_out;

  Pull_Resistor pull_resistor_1 (.node(Reset));
  not not_1 (not_1_out, Stall);
  Clock clock_1 (.out(clock_1_out));
  Pull_Resistor pull_resistor_2 (.node(Stall));
  Register #(.width(32)) register_1 (.D(PC_I), .en(not_1_out), .Q(PC_O), .clk(clock_1_out), .clr(Reset));
  Register #(.width(32)) register_2 (.D(Code_I), .en(not_1_out), .Q(Code_O), .clk(clock_1_out), .clr(Reset));
endmodule

module D_E (
  input  W_I,
  input  Reset,
  input  Clear,
  input  [4:0] A_I,
  input  [31:0] PC_I,
  input  [31:0] D_I,
  input  [2:0] Tnew_I,
  input  [31:0] Code_I,
  input  [4:0] AddrRs_I,
  input  [4:0] AddrRt_I,
  input  [31:0] DataRs_I,
  input  [31:0] DataRt_I,
  input  [4:0] AluOp_I,
  input  [31:0] Imm32_I,
  input  AluSrc1_I,
  input  AluSrc2_I,
  input  [31:0] Shamt32_I,
  input  MemW_I,
  input  [1:0] MSz_I,
  input  MExt_I,
  input  [2:0] WSrc_I,
  output W_O,
  output [4:0] A_O,
  output [31:0] PC_O,
  output [31:0] D_O,
  output [2:0] Tnew_O,
  output [31:0] Code_O,
  output [4:0] AddrRs_O,
  output [4:0] AddrRt_O,
  output [31:0] DataRs_O,
  output [31:0] DataRt_O,
  output [4:0] AluOp_O,
  output [31:0] Imm32_O,
  output AluSrc1_O,
  output AluSrc2_O,
  output [31:0] Shamt32_O,
  output MemW_O,
  output [1:0] MSz_O,
  output MExt_O,
  output [2:0] WSrc_O
);

  wire clock_1_out, clock_2_out, clock_3_out, clock_4_out, clock_5_out, clock_6_out, multiplexer_6_out,
       multiplexer_7_out, multiplexer_8_out, multiplexer_10_out, multiplexer_12_out;
  wire [1:0] multiplexer_9_out;
  wire [2:0] multiplexer_11_out, multiplexer_15_out, subtractor_1_out;
  wire [4:0] multiplexer_3_out, multiplexer_5_out, multiplexer_13_out, multiplexer_16_out;
  wire [31:0] multiplexer_1_out, multiplexer_2_out, multiplexer_4_out, multiplexer_14_out,
       multiplexer_17_out, multiplexer_18_out, multiplexer_19_out;

  Pull_Resistor pull_resistor_1 (.node(Reset));
  Pull_Resistor pull_resistor_2 (.node(Clear));
  Multiplexer #(.width(32), .disabled(0), .enable("false")) multiplexer_1 (
    .in0(PC_I), .in1({32{1'b0}}), .out(multiplexer_1_out), .sel(Clear));
  Multiplexer #(.width(32), .disabled(0), .enable("false")) multiplexer_2 (
    .in0(Code_I), .in1({32{1'b0}}), .out(multiplexer_2_out), .sel(Clear));
  Multiplexer #(.width(5), .disabled(0), .enable("false")) multiplexer_3 (
    .in0(AddrRs_I), .in1({5{1'b0}}), .out(multiplexer_3_out), .sel(Clear));
  Multiplexer #(.width(32), .disabled(0), .enable("false")) multiplexer_4 (
    .in0(DataRs_I), .in1({32{1'b0}}), .out(multiplexer_4_out), .sel(Clear));
  Multiplexer #(.width(5), .disabled(0), .enable("false")) multiplexer_5 (
    .in0(AluOp_I), .in1({5{1'b0}}), .out(multiplexer_5_out), .sel(Clear));
  Multiplexer #(.disabled(0), .enable("false")) multiplexer_6 (
    .in0(AluSrc1_I), .in1(1'b0), .out(multiplexer_6_out), .sel(Clear));
  Multiplexer #(.disabled(0), .enable("false")) multiplexer_7 (
    .in0(AluSrc2_I), .in1(1'b0), .out(multiplexer_7_out), .sel(Clear));
  Multiplexer #(.disabled(0), .enable("false")) multiplexer_8 (
    .in0(MemW_I), .in1(1'b0), .out(multiplexer_8_out), .sel(Clear));
  Multiplexer #(.width(2), .disabled(0), .enable("false")) multiplexer_9 (
    .in0(MSz_I), .in1(2'b00), .out(multiplexer_9_out), .sel(Clear));
  Multiplexer #(.disabled(0), .enable("false")) multiplexer_10 (
    .in0(MExt_I), .in1(1'b0), .out(multiplexer_10_out), .sel(Clear));
  Multiplexer #(.width(3), .disabled(0), .enable("false")) multiplexer_11 (
    .in0(WSrc_I), .in1(3'b000), .out(multiplexer_11_out), .sel(Clear));
  Register #(.width(32)) PC (.D(multiplexer_1_out), .en(1'b1), .Q(PC_O), .clk(clock_1_out), .clr(Reset));
  Register #(.width(32)) Code (.D(multiplexer_2_out), .en(1'b1), .Q(Code_O), .clk(clock_1_out), .clr(Reset));
  Clock clock_1 (.out(clock_1_out));
  Register #(.width(5)) AddrRs (.D(multiplexer_3_out), .en(1'b1), .Q(AddrRs_O), .clk(clock_2_out), .clr(Reset));
  Register #(.width(32)) DataRs (.D(multiplexer_4_out), .en(1'b1), .Q(DataRs_O), .clk(clock_2_out), .clr(Reset));
  Clock clock_2 (.out(clock_2_out));
  Register #(.width(5)) AluOp (.D(multiplexer_5_out), .en(1'b1), .Q(AluOp_O), .clk(clock_3_out), .clr(Reset));
  Register #(.width(1)) AluSrc1 (.D(multiplexer_6_out), .en(1'b1), .Q(AluSrc1_O), .clk(clock_3_out), .clr(Reset));
  Register #(.width(1)) AluSrc2 (.D(multiplexer_7_out), .en(1'b1), .Q(AluSrc2_O), .clk(clock_3_out), .clr(Reset));
  Register #(.width(1)) MemW (.D(multiplexer_8_out), .en(1'b1), .Q(MemW_O), .clk(clock_3_out), .clr(Reset));
  Register #(.width(2)) MSz (.D(multiplexer_9_out), .en(1'b1), .Q(MSz_O), .clk(clock_3_out), .clr(Reset));
  Register #(.width(1)) MExt (.D(multiplexer_10_out), .en(1'b1), .Q(MExt_O), .clk(clock_3_out), .clr(Reset));
  Register #(.width(3)) WSrc (.D(multiplexer_11_out), .en(1'b1), .Q(WSrc_O), .clk(clock_3_out), .clr(Reset));
  Clock clock_3 (.out(clock_3_out));
  Subtractor #(.width(3)) subtractor_1 (.a(Tnew_I), .b(3'b001), .out(subtractor_1_out));  // open: bin, bout
  Multiplexer #(.disabled(0), .enable("false")) multiplexer_12 (
    .in0(W_I), .in1(1'b0), .out(multiplexer_12_out), .sel(Clear));
  Multiplexer #(.width(5), .disabled(0), .enable("false")) multiplexer_13 (
    .in0(A_I), .in1({5{1'b0}}), .out(multiplexer_13_out), .sel(Clear));
  Multiplexer #(.width(32), .disabled(0), .enable("false")) multiplexer_14 (
    .in0(D_I), .in1({32{1'b0}}), .out(multiplexer_14_out), .sel(Clear));
  Multiplexer #(.width(3), .disabled(0), .enable("false")) multiplexer_15 (
    .in0(subtractor_1_out), .in1(3'b000), .out(multiplexer_15_out), .sel(Clear));
  Multiplexer #(.width(5), .disabled(0), .enable("false")) multiplexer_16 (
    .in0(AddrRt_I), .in1({5{1'b0}}), .out(multiplexer_16_out), .sel(Clear));
  Multiplexer #(.width(32), .disabled(0), .enable("false")) multiplexer_17 (
    .in0(DataRt_I), .in1({32{1'b0}}), .out(multiplexer_17_out), .sel(Clear));
  Multiplexer #(.width(32), .disabled(0), .enable("false")) multiplexer_18 (
    .in0(Imm32_I), .in1({32{1'b0}}), .out(multiplexer_18_out), .sel(Clear));
  Multiplexer #(.width(32), .disabled(0), .enable("false")) multiplexer_19 (
    .in0(Shamt32_I), .in1({32{1'b0}}), .out(multiplexer_19_out), .sel(Clear));
  Register #(.width(1)) W (.D(multiplexer_12_out), .en(1'b1), .Q(W_O), .clk(clock_4_out), .clr(Reset));
  Register #(.width(5)) A (.D(multiplexer_13_out), .en(1'b1), .Q(A_O), .clk(clock_4_out), .clr(Reset));
  Register #(.width(32)) D (.D(multiplexer_14_out), .en(1'b1), .Q(D_O), .clk(clock_4_out), .clr(Reset));
  Register #(.width(3)) Tnew (.D(multiplexer_15_out), .en(1'b1), .Q(Tnew_O), .clk(clock_4_out), .clr(Reset));
  Clock clock_4 (.out(clock_4_out));
  Register #(.width(5)) AddrRt (.D(multiplexer_16_out), .en(1'b1), .Q(AddrRt_O), .clk(clock_5_out), .clr(Reset));
  Register #(.width(32)) DataRt (.D(multiplexer_17_out), .en(1'b1), .Q(DataRt_O), .clk(clock_5_out), .clr(Reset));
  Clock clock_5 (.out(clock_5_out));
  Register #(.width(32)) Imm32 (.D(multiplexer_18_out), .en(1'b1), .Q(Imm32_O), .clk(clock_6_out), .clr(Reset));
  Register #(.width(32)) Shamt32 (.D(multiplexer_19_out), .en(1'b1), .Q(Shamt32_O), .clk(clock_6_out), .clr(Reset));
  Clock clock_6 (.out(clock_6_out));
endmodule

module E_M (
  input  W_I,
  input  Reset,
  input  [4:0] A_I,
  input  [31:0] PC_I,
  input  [31:0] D_I,
  input  [2:0] Tnew_I,
  input  [31:0] Code_I,
  input  [4:0] AddrRt_I,
  input  MemW_I,
  input  [1:0] MSz_I,
  input  [31:0] DataRt_I,
  input  MExt_I,
  input  [31:0] AluOut_I,
  input  [2:0] WSrc_I,
  output W_O,
  output [4:0] A_O,
  output [31:0] PC_O,
  output [31:0] D_O,
  output [2:0] Tnew_O,
  output [31:0] Code_O,
  output [4:0] AddrRt_O,
  output MemW_O,
  output [1:0] MSz_O,
  output [31:0] DataRt_O,
  output MExt_O,
  output [31:0] AluOut_O,
  output [2:0] WSrc_O
);

  wire clock_1_out, clock_2_out, clock_3_out, clock_4_out, clock_5_out, clock_6_out;
  wire [2:0] subtractor_1_out;

  Pull_Resistor pull_resistor_1 (.node(Reset));
  Clock clock_1 (.out(clock_1_out));
  Clock clock_2 (.out(clock_2_out));
  Clock clock_3 (.out(clock_3_out));
  Register #(.width(32)) PC (.D(PC_I), .en(1'b1), .Q(PC_O), .clk(clock_1_out), .clr(Reset));
  Register #(.width(32)) Code (.D(Code_I), .en(1'b1), .Q(Code_O), .clk(clock_1_out), .clr(Reset));
  Register #(.width(5)) AddrRt (.D(AddrRt_I), .en(1'b1), .Q(AddrRt_O), .clk(clock_2_out), .clr(Reset));
  Register #(.width(32)) DataRt (.D(DataRt_I), .en(1'b1), .Q(DataRt_O), .clk(clock_2_out), .clr(Reset));
  Register #(.width(32)) AluOut (.D(AluOut_I), .en(1'b1), .Q(AluOut_O), .clk(clock_3_out), .clr(Reset));
  Subtractor #(.width(3)) subtractor_1 (.a(Tnew_I), .b(3'b001), .out(subtractor_1_out));  // open: bin, bout
  Register #(.width(1)) W (.D(W_I), .en(1'b1), .Q(W_O), .clk(clock_4_out), .clr(Reset));
  Register #(.width(5)) A (.D(A_I), .en(1'b1), .Q(A_O), .clk(clock_4_out), .clr(Reset));
  Register #(.width(32)) D (.D(D_I), .en(1'b1), .Q(D_O), .clk(clock_4_out), .clr(Reset));
  Register #(.width(3)) Tnew (.D(subtractor_1_out), .en(1'b1), .Q(Tnew_O), .clk(clock_4_out), .clr(Reset));
  Clock clock_4 (.out(clock_4_out));
  Register #(.width(1)) MemW (.D(MemW_I), .en(1'b1), .Q(MemW_O), .clk(clock_5_out), .clr(Reset));
  Register #(.width(2)) MSz (.D(MSz_I), .en(1'b1), .Q(MSz_O), .clk(clock_5_out), .clr(Reset));
  Register #(.width(1)) MExt (.D(MExt_I), .en(1'b1), .Q(MExt_O), .clk(clock_5_out), .clr(Reset));
  Clock clock_5 (.out(clock_5_out));
  Register #(.width(3)) WSrc (.D(WSrc_I), .en(1'b1), .Q(WSrc_O), .clk(clock_6_out), .clr(Reset));
  Clock clock_6 (.out(clock_6_out));
endmodule

module M_W (
  input  Reset,
  input  W_I,
  input  [31:0] PC_I,
  input  [4:0] A_I,
  input  [31:0] Code_I,
  input  [31:0] D_I,
  input  [2:0] WSrc_I,
  input  [31:0] MRD_I,
  input  [1:0] Off_I,
  input  [1:0] MSz_I,
  input  MExt_I,
  output W_O,
  output [31:0] PC_O,
  output [4:0] A_O,
  output [31:0] Code_O,
  output [31:0] D_O,
  output [2:0] WSrc_O,
  output [31:0] MRD_O,
  output [1:0] Off_O,
  output [1:0] MSz_O,
  output MExt_O
);

  wire clock_1_out, clock_2_out, clock_3_out, clock_4_out;

  Pull_Resistor pull_resistor_1 (.node(Reset));
  Clock clock_1 (.out(clock_1_out));
  Clock clock_2 (.out(clock_2_out));
  Register #(.width(32)) PC (.D(PC_I), .en(1'b1), .Q(PC_O), .clk(clock_1_out), .clr(Reset));
  Register #(.width(32)) Code (.D(Code_I), .en(1'b1), .Q(Code_O), .clk(clock_1_out), .clr(Reset));
  Register #(.width(32)) MRD (.D(MRD_I), .en(1'b1), .Q(MRD_O), .clk(clock_2_out), .clr(Reset));
  Register #(.width(2)) Offset (.D(Off_I), .en(1'b1), .Q(Off_O), .clk(clock_2_out), .clr(Reset));
  Register #(.width(2)) MSz (.D(MSz_I), .en(1'b1), .Q(MSz_O), .clk(clock_2_out), .clr(Reset));
  Register #(.width(1)) MExt (.D(MExt_I), .en(1'b1), .Q(MExt_O), .clk(clock_2_out), .clr(Reset));
  Register #(.width(1)) W (.D(W_I), .en(1'b1), .Q(W_O), .clk(clock_3_out), .clr(Reset));
  Register #(.width(5)) A (.D(A_I), .en(1'b1), .Q(A_O), .clk(clock_3_out), .clr(Reset));
  Register #(.width(32)) D (.D(D_I), .en(1'b1), .Q(D_O), .clk(clock_3_out), .clr(Reset));
  Clock clock_3 (.out(clock_3_out));
  Register #(.width(3)) WSrc (.D(WSrc_I), .en(1'b1), .Q(WSrc_O), .clk(clock_4_out), .clr(Reset));
  Clock clock_4 (.out(clock_4_out));
endmodule

module CPU (
  input  Reset,
  input  [31:0] I_Data,
  input  [31:0] D_RData,
  output [11:0] I_Addr,
  output [31:0] PC_F,
  output [31:0] PC_D,
  output [11:0] D_Addr,
  output W,
  output [31:0] PC_E,
  output [3:0] D_ByteEn,
  output [4:0] A,
  output [31:0] D_WData,
  output [31:0] PC_M,
  output [31:0] D,
  output [31:0] PC_W
);

  wire AluSrc1_D, AluSrc1_E, AluSrc2_D, AluSrc2_E, Flag_D, MemW_D, MemW_E, MemW_M, MExt_D, MExt_E, MExt_M,
       MExt_W, RegW_D, Stall, UseRs_D, UseRt_D, W_E, W_M;
  wire [1:0] ExtOp_D, MSz_D, MSz_E, MSz_M, MSz_W, Off_M, Off_W;
  wire [2:0] NpcOp_D, Tnew_D, Tnew_E, Tnew_M, TuseRs_D, TuseRt_D, WDst_D, WSrc_D, WSrc_E, WSrc_M, WSrc_W;
  wire [4:0] A_D, A_E, A_M, AddrRd_D, AddrRs_D, AddrRs_E, AddrRt_D, AddrRt_E, AddrRt_M, AluOp_D, AluOp_E,
       CmpOp_D, Shamt5_D;
  wire [15:0] Imm16_D;
  wire [25:0] Imm26_D;
  wire [31:0] adder_1_out, AluOut_E, AluOut_M, Code_D, Code_E, Code_M, Code_W, D_D, D_E, D_M, DataRs_D,
       DataRs_E, DataRt_D, DataRt_E, DataRt_M, FwdRs_D, FwdRs_E, FwdRt_D, FwdRt_E, Imm32_D, Imm32_E,
       m_w_1_d_o, MRead_W, multiplexer_4_out, multiplexer_5_out, pull_resistor_3_node, RData_W, Shamt32_D,
       Shamt32_E, subtractor_1_out;

  // Probe on nothing
  // Probe on PC_F
  PC pc_1 (
    .Br(Imm16_D), .reset(Reset), .Jmp(Imm26_D), .Stall(Stall), .NpcOp(NpcOp_D), .Ra(FwdRs_D), .Flag(Flag_D),
    .PC(PC_F));  // open: NPC
  Subtractor #(.width(32)) subtractor_1 (
    .a(PC_F), .b(32'h3000), .out({subtractor_1_out[31:14], I_Addr, subtractor_1_out[1:0]}));  // open: bin, bout
  F_D f_d_1 (.Reset(Reset), .Stall(Stall), .PC_I(PC_F), .Code_I(I_Data), .PC_O(PC_D), .Code_O(Code_D));
  // Probe on PC_D
  Adder #(.width(32)) adder_1 (.a(PC_D), .b(32'h8), .out(adder_1_out));  // open: cin, cout
  Pull_Resistor pull_resistor_1 (.node(A_D));
  Multiplexer #(.select(3), .width(5), .disabled(0), .enable("false")) multiplexer_1 (
    .in0(AddrRd_D), .in1(AddrRt_D), .in2({5{1'b1}}), .out(A_D), .sel(WDst_D));  // open: in3, in4, in5, in6, in7
  Pull_Resistor pull_resistor_2 (.node(D_D));
  Multiplexer #(.select(3), .width(32), .disabled(0), .enable("false")) multiplexer_2 (
    .in0(adder_1_out), .in1(Imm32_D), .out(D_D), .sel(WSrc_D));  // open: in2, in3, in4, in5, in6, in7
  // Probe on PC_E
  GRF grf_1 (
    .RAddr1(AddrRs_D), .RAddr2(AddrRt_D), .reset(Reset), .WE(W), .WAddr(A), .WData(D), .RData1(DataRs_D),
    .RData2(DataRt_D));
  D_E d_e_1 (
    .W_I(RegW_D), .Reset(Reset), .Clear(Stall), .A_I(A_D), .PC_I(PC_D), .D_I(D_D), .Tnew_I(Tnew_D),
    .Code_I(Code_D), .AddrRs_I(AddrRs_D), .AddrRt_I(AddrRt_D), .DataRs_I(FwdRs_D), .DataRt_I(FwdRt_D),
    .AluOp_I(AluOp_D), .AluSrc1_I(AluSrc1_D), .AluSrc2_I(AluSrc2_D), .MemW_I(MemW_D), .MExt_I(MExt_D),
    .W_O(W_E), .A_O(A_E), .PC_O(PC_E), .D_O(D_E), .Tnew_O(Tnew_E), .Code_O(Code_E), .AddrRs_O(AddrRs_E),
    .AddrRt_O(AddrRt_E), .DataRs_O(DataRs_E), .DataRt_O(DataRt_E), .AluOp_O(AluOp_E), .AluSrc1_O(AluSrc1_E),
    .AluSrc2_O(AluSrc2_E), .MemW_O(MemW_E), .MSz_O(MSz_E), .MExt_O(MExt_E), .Imm32_I(Imm32_D),
    .Imm32_O(Imm32_E), .Shamt32_I(Shamt32_D), .Shamt32_O(Shamt32_E), .MSz_I(MSz_D), .WSrc_I(WSrc_D),
    .WSrc_O(WSrc_E));
  Controller controller_1 (
    .Code(Code_D), .UseRs(UseRs_D), .AluOp(AluOp_D), .AddrRs(AddrRs_D), .TuseRs(TuseRs_D), .CmpOp(CmpOp_D),
    .NpcOp(NpcOp_D), .UseRt(UseRt_D), .ExtOp(ExtOp_D), .AddrRt(AddrRt_D), .TuseRt(TuseRt_D),
    .AluSrc1(AluSrc1_D), .RegW(RegW_D), .AluSrc2(AluSrc2_D), .Tnew(Tnew_D), .WDst(WDst_D), .MemW(MemW_D),
    .WSrc(WSrc_D), .MSz(MSz_D), .AddrRd(AddrRd_D), .MExt(MExt_D), .Imm16(Imm16_D), .Imm26(Imm26_D),
    .Shamt(Shamt5_D));
  // Probe on PC_M
  CMP cmp_1 (.Src1(FwdRs_D), .CmpOp(CmpOp_D), .Src2(FwdRt_D), .Flag(Flag_D));
  EXT ext_1 (.In(Imm16_D), .ExtOp(ExtOp_D), .out_3(Imm32_D));
  assign Shamt32_D = {{27{1'b0}}, Shamt5_D};  // Bit_Extender bit_extender_1
  // Probe on PC_W
  Pull_Resistor pull_resistor_3 (.node(pull_resistor_3_node));
  Multiplexer #(.select(3), .width(32), .disabled(0), .enable("false")) multiplexer_3 (
    .in0(D_E), .in1(D_E), .in2(AluOut_E), .out(pull_resistor_3_node), .sel(WSrc_E));  // open: in3, in4, in5, in6, in7
  Multiplexer #(.width(32), .disabled(0), .enable("false")) multiplexer_4 (
    .in0(FwdRs_E), .in1(Shamt32_E), .out(multiplexer_4_out), .sel(AluSrc1_E));
  Multiplexer #(.width(32), .disabled(0), .enable("false")) multiplexer_5 (
    .in0(FwdRt_E), .in1(Imm32_E), .out(multiplexer_5_out), .sel(AluSrc2_E));
  E_M e_m_1 (
    .W_I(W_E), .Reset(Reset), .A_I(A_E), .PC_I(PC_E), .D_I(pull_resistor_3_node), .Code_I(Code_E),
    .AddrRt_I(AddrRt_E), .MemW_I(MemW_E), .MSz_I(MSz_E), .DataRt_I(FwdRt_E), .MExt_I(MExt_E),
    .AluOut_I(AluOut_E), .W_O(W_M), .A_O(A_M), .PC_O(PC_M), .D_O(D_M), .Code_O(Code_M), .AddrRt_O(AddrRt_M),
    .MemW_O(MemW_M), .MSz_O(MSz_M), .DataRt_O(DataRt_M), .MExt_O(MExt_M), .AluOut_O(AluOut_M),
    .Tnew_I(Tnew_E), .Tnew_O(Tnew_M), .WSrc_I(WSrc_E), .WSrc_O(WSrc_M));
  ALU alu_1 (.Src1(multiplexer_4_out), .AluOp(AluOp_E), .Src2(multiplexer_5_out), .Out(AluOut_E));
  StallUnit stallunit_1 (
    .UseRs_D(UseRs_D), .UseRt_D(UseRt_D), .W_E(W_E), .W_M(W_M), .AddrRs_D(AddrRs_D), .AddrRt_D(AddrRt_D),
    .A_E(A_E), .A_M(A_M), .TuseRs_D(TuseRs_D), .TuseRt_D(TuseRt_D), .Tnew_E(Tnew_E), .Tnew_M(Tnew_M),
    .Stall(Stall));
  M_W m_w_1 (
    .W_I(W_M), .Reset(Reset), .A_I(A_M), .PC_I(PC_M), .D_I(D_M), .Code_I(Code_M), .MRD_I(D_RData),
    .Off_I(Off_M), .MSz_I(MSz_M), .MExt_I(MExt_M), .W_O(W), .A_O(A), .PC_O(PC_W), .D_O(m_w_1_d_o),
    .Code_O(Code_W), .MRD_O(RData_W), .Off_O(Off_W), .MSz_O(MSz_W), .MExt_O(MExt_W), .WSrc_I(WSrc_M),
    .WSrc_O(WSrc_W));
  MemAddr memaddr_1 (.Addr(AluOut_M), .Scale(MSz_M), .MemW(MemW_M), .ByteEn(D_ByteEn), .MAddr(D_Addr), .Offset(Off_M));
  Pull_Resistor pull_resistor_4 (.node(D));
  Multiplexer #(.select(3), .width(32), .disabled(0), .enable("false")) multiplexer_6 (
    .in0(m_w_1_d_o), .in1(m_w_1_d_o), .in2(m_w_1_d_o), .in3(MRead_W), .out(D), .sel(WSrc_W));  // open: in4, in5, in6, in7
  ForwardUnit u_FwdRs_D (
    .W1(W_E), .W2(W_M), .A0(AddrRs_D), .A1(A_E), .A2(A_M), .D0(DataRs_D), .D1(D_E), .D2(D_M), .D(FwdRs_D));  // open: NoFwd, Fwd1, Fwd2
  ForwardUnit u_FwdRt_D (
    .W1(W_E), .W2(W_M), .A0(AddrRt_D), .A1(A_E), .A2(A_M), .D0(DataRt_D), .D1(D_E), .D2(D_M), .D(FwdRt_D));  // open: NoFwd, Fwd1, Fwd2
  ForwardUnit u_FwdRs_E (
    .W1(W_M), .W2(W), .A0(AddrRs_E), .A1(A_M), .A2(A), .D0(DataRs_E), .D1(D_M), .D2(D), .D(FwdRs_E));  // open: NoFwd, Fwd1, Fwd2
  ForwardUnit u_FwdRt_E (
    .W1(W_M), .W2(W), .A0(AddrRt_E), .A1(A_M), .A2(A), .D0(DataRt_E), .D1(D_M), .D2(D), .D(FwdRt_E));  // open: NoFwd, Fwd1, Fwd2
  ForwardUnit FwdRt_M (
    .W1(W), .A0(AddrRt_M), .A1(A), .D0(DataRt_M), .D1(D), .D(D_WData));  // open: W2, A2, D2, NoFwd, Fwd1, Fwd2
  MemExt memext_1 (.MWord(RData_W), .Offset(Off_W), .Ext(MExt_W), .Sz(MSz_W), .MRead(MRead_W));
  // Probe on nothing

  // Other names for the same wires on the sheet: A_W[4:0] = A; D_W[31:0] = D; FwdRt_M[31:0] = D_WData; W_D = RegW_D;
  //   W_W = W

  // Notes on the sheet:
  //   CPU-Ports
endmodule

module main (
  input  Reset,
  output [31:0] pc_w,
  output [31:0] pc_m,
  output RegWrite,
  output [4:0] RegAddr,
  output [31:0] RegData,
  output MemWrite,
  output [31:0] MemAddr,
  output [31:0] MemData
);

  wire [3:0] cpu_1_d_byteen;
  wire [11:0] cpu_1_d_addr, cpu_1_i_addr;
  wire [31:0] bit_extender_1_out, dm_1_dout, rom_1_data;

  CPU cpu_1 (
    .Reset(Reset), .I_Data(rom_1_data), .D_RData(dm_1_dout), .I_Addr(cpu_1_i_addr), .D_Addr(cpu_1_d_addr),
    .W(RegWrite), .D_ByteEn(cpu_1_d_byteen), .A(RegAddr), .D_WData(MemData), .PC_M(pc_m), .D(RegData),
    .PC_W(pc_w));  // open: PC_F, PC_D, PC_E
  ROM #(.addrWidth(12), .dataWidth(32)) rom_1 (.addr(cpu_1_i_addr), .data(rom_1_data), .sel(1'b1));
  assign bit_extender_1_out = {{20{1'b0}}, cpu_1_d_addr};  // Bit_Extender bit_extender_1
  or or_1 (MemWrite, cpu_1_d_byteen[0], cpu_1_d_byteen[1], cpu_1_d_byteen[2], cpu_1_d_byteen[3]);
  Shifter #(.width(32)) shifter_1 (.in(bit_extender_1_out), .\dist (5'b00010), .out(MemAddr));
  DM dm_1 (.A(cpu_1_d_addr), .DIn(MemData), .ByteEn(cpu_1_d_byteen), .DOut(dm_1_dout), .Reset(Reset));

  // Notes on the sheet:
  //   contents of rom_1 (hex, n*v repeats v):
  //   341c0000 341d0000 34011010 3c028723 34037856 3c0485ff 34050001 3c06ffff 34e7ffff 220821 234821
  //   224023 e00023 13910003 0 8000c25 0 10220013 0 3402000c 0 0 0 c000c1b ac410000 8000c25 4*220821
  //   ac5f0000 8c410000 0 0 0 200008 ac5f0000 1000ffff
endmodule
